// Logisim project 8_clock_delay.circ as structural Verilog: 1 circuit, main circuit eightClockDelay
module eightClockDelay (
  input  [31:0] DataIn,
  input  clk,
  output [31:0] DataOut
);

  wire [31:0] register_1_q, register_2_q, register_3_q, register_4_q, register_5_q, register_6_q,
       register_7_q;

  Register #(.width(32)) register_1 (.D(DataIn), .clk(clk), .Q(register_1_q));  // open: en, clr
  Register #(.width(32)) register_2 (.D(register_1_q), .clk(clk), .Q(register_2_q));  // open: en, clr
  Register #(.width(32)) register_3 (.D(register_2_q), .clk(clk), .Q(register_3_q));  // open: en, clr
  Register #(.width(32)) register_4 (.D(register_3_q), .clk(clk), .Q(register_4_q));  // open: en, clr
  Register #(.width(32)) register_5 (.D(register_4_q), .clk(clk), .Q(register_5_q));  // open: en, clr
  Register #(.width(32)) register_6 (.D(register_5_q), .clk(clk), .Q(register_6_q));  // open: en, clr
  Register #(.width(32)) register_7 (.D(register_6_q), .clk(clk), .Q(register_7_q));  // open: en, clr
  Register #(.width(32)) register_8 (.D(register_7_q), .clk(clk), .Q(DataOut));  // open: en, clr
endmodule
