// Logisim project ALUController.circ as structural Verilog: 1 circuit, main circuit main
module main (
  input  [5:0] func,
  input  [5:0] opcode,
  input  aluOperation,
  output [4:0] r_map_out,
  output [4:0] i_j_map_out,
  output [4:0] aluC_out
);

  wire a_not, and_1_out, and_2_out, and_3_out, and_4_out, and_5_out, and_6_out, and_7_out, and_8_out,
       and_9_out, and_10_out, and_11_out, and_12_out, and_13_out, and_14_out, and_15_out, and_16_out,
       and_17_out, and_18_out, and_19_out, and_20_out, and_21_out, and_22_out, and_23_out, and_24_out,
       and_25_out, and_26_out, and_27_out, and_28_out, and_29_out, and_30_out, b_not, c_not, d_not, e_not,
       f_not, in1_not, in2_not, in3_not, in4_not, in5_not, in6_not, or_2_out, or_3_out, or_4_out, or_5_out,
       or_6_out, or_7_out, or_12_out, or_13_out, or_14_out, or_18_out, or_19_out, or_20_out;
  wire [4:0] i_j_map_out_t, multiplexer_1_out, r_map_out_t;

  not not_1 (a_not, func[5]);
  not not_2 (b_not, func[4]);
  not not_3 (c_not, func[3]);
  not not_4 (d_not, func[2]);
  not not_5 (e_not, func[1]);
  not not_6 (f_not, func[0]);
  not not_7 (in1_not, opcode[5]);
  not not_8 (in2_not, opcode[4]);
  not not_9 (in3_not, opcode[3]);
  not not_10 (in4_not, opcode[2]);
  not not_11 (in5_not, opcode[1]);
  not not_12 (in6_not, opcode[0]);
  and and_1 (and_1_out, func[5], func[3]);
  and and_2 (and_2_out, func[2], func[1], func[0]);
  and and_3 (and_3_out, func[2], func[5]);
  and and_4 (and_4_out, func[2], f_not);
  and and_5 (and_5_out, a_not, func[2]);
  and and_6 (and_6_out, func[0], a_not);
  and and_7 (and_7_out, func[5], func[1], c_not, f_not);
  and and_8 (and_8_out, d_not, func[3]);
  and and_9 (and_9_out, c_not, a_not, func[2]);
  and and_10 (and_10_out, func[4], func[1]);
  and and_11 (and_11_out, func[5], d_not, func[0]);
  and and_12 (and_12_out, func[1], b_not, d_not);
  or or_1 (r_map_out[4], and_1_out, and_2_out);
  or or_2 (or_2_out, f_not, d_not);
  and and_13 (and_13_out, func[5], c_not);
  or or_3 (or_3_out, func[3], and_3_out);
  or or_4 (or_4_out, and_11_out, and_4_out);
  or or_5 (or_5_out, func[4], and_5_out, func[0]);
  or or_6 (or_6_out, func[5], and_12_out);
  or or_7 (or_7_out, and_8_out, and_9_out);
  and and_14 (and_14_out, e_not, func[0]);
  and and_15 (and_15_out, or_2_out, and_13_out);
  and and_16 (and_16_out, e_not, or_3_out);
  and and_17 (and_17_out, or_4_out, func[1]);
  and and_18 (and_18_out, e_not, or_5_out);
  and and_19 (and_19_out, f_not, or_6_out);
  and and_20 (and_20_out, or_7_out, e_not);
  or or_8 (r_map_out[3], and_10_out, and_14_out, and_15_out);
  or or_9 (r_map_out[2], and_16_out, and_17_out);
  or or_10 (r_map_out[1], and_18_out, and_6_out, and_7_out);
  or or_11 (r_map_out[0], and_19_out, and_20_out);
  or or_12 (or_12_out, in3_not, in5_not);
  or or_13 (or_13_out, in5_not, in6_not);
  or or_14 (or_14_out, in4_not, opcode[0]);
  and and_21 (and_21_out, opcode[3], opcode[2]);
  and and_22 (and_22_out, in1_not, in4_not, or_12_out);
  and and_23 (and_23_out, opcode[2], or_13_out);
  and and_24 (and_24_out, in1_not, in3_not, opcode[1], opcode[0]);
  and and_25 (and_25_out, or_14_out, opcode[1]);
  or or_15 (i_j_map_out[3], and_21_out, and_22_out);
  or or_16 (i_j_map_out[4], in3_not, opcode[5], and_25_out);
  or or_17 (i_j_map_out[2], and_23_out, and_24_out);
  Multiplexer #(.width(5)) multiplexer_1 (
    .in0(i_j_map_out_t), .in1(r_map_out_t), .out(multiplexer_1_out), .sel(aluOperation));
  and and_26 (and_26_out, in4_not, in6_not, in3_not);
  or or_18 (or_18_out, in3_not, in6_not);
  and and_27 (and_27_out, opcode[3], in5_not, opcode[0]);
  or or_19 (or_19_out, in4_not, opcode[3]);
  or or_20 (or_20_out, in3_not, opcode[1]);
  and and_28 (and_28_out, or_18_out, opcode[2], opcode[1]);
  and and_29 (and_29_out, in6_not, or_19_out);
  and and_30 (and_30_out, or_20_out, opcode[2], opcode[0]);
  or or_21 (i_j_map_out[1], opcode[5], and_26_out, and_28_out, and_27_out);
  or or_22 (i_j_map_out[0], and_29_out, and_30_out);

  // Other names for the same wires on the sheet: f = func[0]; e = func[1]; d = func[2]; c = func[3]; b = func[4];
  //   a = func[5]; N5 = i_j_map_out[0]; N4 = i_j_map_out[1]; N3 = i_j_map_out[2]; N2 = i_j_map_out[3];
  //   N1 = i_j_map_out[4]; in6 = opcode[0]; in5 = opcode[1]; in4 = opcode[2]; in3 = opcode[3]; in2 = opcode[4];
  //   in1 = opcode[5]; M5 = r_map_out[0]; M4 = r_map_out[1]; M3 = r_map_out[2]; M2 = r_map_out[3]; M1 = r_map_out[4]

  // Notes on the sheet:
  //   r type
  //   i and j type
endmodule
