// Logisim project Control.circ as structural Verilog: 1 circuit, main circuit Controller
module Controller (
  input  [5:0] Opcode,
  output RegDst,
  output Branch,
  output Jump,
  output RegWrEn,
  output AluSrc,
  output MemToReg,
  output AluOpr,
  output [3:0] MemWrMask,
  output LB,
  output CacheAccess
);

  wire and_2_out, and_3_out, and_5_out, and_6_out, and_7_out, comparator_2_eq, comparator_3_eq, I0_N, I1_N,
       I2_N, I3_N, I4_N, I5_N;

  and and_1 (RegDst, I5_N, I3_N);
  and and_2 (and_2_out, Opcode[0], I1_N, I3_N);
  and and_3 (and_3_out, I3_N, Opcode[2]);
  and and_4 (Jump, I5_N, I3_N, I2_N, Opcode[1]);
  and and_5 (and_5_out, I5_N, Opcode[3]);
  and and_6 (and_6_out, Opcode[1], Opcode[0], I3_N, I2_N);
  and and_7 (and_7_out, I3_N, I2_N, I1_N, I0_N);
  or or_1 (Branch, and_2_out, and_3_out);
  or or_2 (RegWrEn, and_5_out, and_6_out, and_7_out);
  or or_3 (AluSrc, Opcode[5], Opcode[3], Opcode[2], Opcode[0]);
  and and_8 (MemWrMask[0], Opcode[3], Opcode[5]);
  and and_9 (MemWrMask[3], Opcode[3], Opcode[5], Opcode[0]);
  nor nor_1 (AluOpr, Opcode[5], Opcode[0], Opcode[2], Opcode[3], Opcode[1]);
  not not_1 (I5_N, Opcode[5]);
  not not_2 (I4_N, Opcode[4]);
  not not_3 (I3_N, Opcode[3]);
  not not_4 (I2_N, Opcode[2]);
  not not_5 (I1_N, Opcode[1]);
  not not_6 (I0_N, Opcode[0]);
  Comparator #(.width(6)) comparator_1 (.a(Opcode), .b(6'b100000), .eq(LB));  // open: gt, lt
  Comparator #(.width(6)) comparator_2 (.a(Opcode), .b(6'b101011), .eq(comparator_2_eq));  // open: gt, lt
  Comparator #(.width(6)) comparator_3 (.a(Opcode), .b(6'b100011), .eq(comparator_3_eq));  // open: gt, lt
  or or_4 (CacheAccess, comparator_2_eq, comparator_3_eq);

  assign MemToReg = Opcode[5];
  assign MemWrMask[2:1] = {2{MemWrMask[3]}};

  // Other names for the same wires on the sheet: I0 = Opcode[0]; I1 = Opcode[1]; I2 = Opcode[2]; I3 = Opcode[3];
  //   I4 = Opcode[4]; I5 = Opcode[5]
endmodule
