// Logisim project EX_MEM2.circ as structural Verilog: 1 circuit, main circuit EX_MEM_PC
module EX_MEM_PC (
  input  Clock,
  input  [31:0] J_PCIN,
  input  [31:0] PCIN,
  input  [31:0] BR_PCIN,
  input  Freeze,
  output [31:0] J_PCOUT,
  output [31:0] PCOUT,
  output [31:0] BR_PCOUT
);

  wire xor_1_out;

  xor xor_1 (xor_1_out, 1'b1, Freeze);
  Register #(.width(32)) register_1 (.D(J_PCIN), .en(xor_1_out), .clk(Clock), .Q(J_PCOUT));  // open: clr
  Register #(.width(32)) register_2 (.D(PCIN), .en(xor_1_out), .clk(Clock), .Q(PCOUT));  // open: clr
  Register #(.width(32)) register_3 (.D(BR_PCIN), .en(xor_1_out), .clk(Clock), .Q(BR_PCOUT));  // open: clr
endmodule
