// Logisim project ID_EX.circ as structural Verilog: 1 circuit, main circuit ID_EX
module ID_EX (
  input  clk,
  input  RegDstIn,
  input  BranchIn,
  input  JumpIn,
  input  RegWrEnIn,
  input  AluSrcIn,
  input  MemToRegIn,
  input  AluOprIn,
  input  [3:0] MemWrMaskIn,
  input  LBIn,
  input  [31:0] ReadData1In,
  input  [31:0] ReadData2In,
  input  [31:0] extendedBitsIn,
  input  [31:0] ExtendedIn,
  input  [4:0] ALu_outIn,
  input  sh_amountIn,
  input  [4:0] WrIdxIn,
  input  reset,
  input  CAccIn,
  input  Frz,
  output RegDstOut,
  output BranchOut,
  output JumpOut,
  output RegWrEnOut,
  output AluSrcOut,
  output MemToRegOut,
  output AluOprOut,
  output [3:0] MemWrMaskOut,
  output LBOut,
  output [31:0] ReadData1Out,
  output [31:0] ReadData2Out,
  output [31:0] extendedBitsOut,
  output [31:0] ExtendedOut,
  output [4:0] Alu_outOut,
  output sh_amountOut,
  output [4:0] WrIdxOut,
  output CAccOut
);

  wire xor_1_out;

  xor xor_1 (xor_1_out, Frz, 1'b1);
  Register #(.width(1)) register_1 (.D(RegDstIn), .en(xor_1_out), .clk(clk), .Q(RegDstOut), .clr(reset));
  Register #(.width(1)) register_2 (.D(BranchIn), .en(xor_1_out), .clk(clk), .Q(BranchOut), .clr(reset));
  Register #(.width(1)) register_3 (.D(JumpIn), .en(xor_1_out), .clk(clk), .Q(JumpOut), .clr(reset));
  Register #(.width(1)) register_4 (.D(RegWrEnIn), .en(xor_1_out), .clk(clk), .Q(RegWrEnOut), .clr(reset));
  Register #(.width(1)) register_5 (.D(AluSrcIn), .en(xor_1_out), .clk(clk), .Q(AluSrcOut), .clr(reset));
  Register #(.width(1)) register_6 (.D(MemToRegIn), .en(xor_1_out), .clk(clk), .Q(MemToRegOut), .clr(reset));
  Register #(.width(1)) register_7 (.D(AluOprIn), .en(xor_1_out), .clk(clk), .Q(AluOprOut), .clr(reset));
  Register #(.width(4)) register_8 (.D(MemWrMaskIn), .en(xor_1_out), .clk(clk), .Q(MemWrMaskOut), .clr(reset));
  Register #(.width(1)) register_9 (.D(LBIn), .en(xor_1_out), .clk(clk), .Q(LBOut), .clr(reset));
  Register #(.width(32)) register_10 (.D(ReadData1In), .en(xor_1_out), .clk(clk), .Q(ReadData1Out), .clr(reset));
  Register #(.width(32)) register_11 (.D(ReadData2In), .en(xor_1_out), .clk(clk), .Q(ReadData2Out), .clr(reset));
  Register #(.width(32)) register_12 (.D(extendedBitsIn), .en(xor_1_out), .clk(clk), .Q(extendedBitsOut), .clr(reset));
  Register #(.width(32)) register_13 (.D(ExtendedIn), .en(xor_1_out), .clk(clk), .Q(ExtendedOut), .clr(reset));
  Register #(.width(5)) register_14 (.D(ALu_outIn), .en(xor_1_out), .clk(clk), .Q(Alu_outOut), .clr(reset));
  Register #(.width(1)) register_15 (.D(sh_amountIn), .en(xor_1_out), .clk(clk), .Q(sh_amountOut), .clr(reset));
  Register #(.width(5)) register_16 (.D(WrIdxIn), .en(xor_1_out), .clk(clk), .Q(WrIdxOut), .clr(reset));
  Register #(.width(1)) register_17 (.D(CAccIn), .en(xor_1_out), .clk(clk), .Q(CAccOut));  // open: clr
endmodule
