// Logisim project ID_EX2.circ as structural Verilog: 1 circuit, main circuit ID_EX_PC
module ID_EX_PC (
  input  Clock,
  input  [31:0] J_PCIN,
  input  [31:0] PCIn,
  input  Frz,
  input  reset,
  output [31:0] J_PCOUT,
  output [31:0] PCOut
);

  wire xor_1_out;

  xor xor_1 (xor_1_out, Frz, 1'b1);
  Register #(.width(32)) register_1 (.D(J_PCIN), .en(xor_1_out), .clk(Clock), .Q(J_PCOUT), .clr(reset));
  Register #(.width(32)) register_2 (.D(PCIn), .en(xor_1_out), .clk(Clock), .Q(PCOut), .clr(reset));
endmodule
