// Logisim project MEMDB.circ as structural Verilog: 1 circuit, main circuit MEM_WB
module MEM_WB (
  input  Clock,
  input  [31:0] CacheReadDataIn,
  input  MemToRegIn,
  input  JumpIn,
  input  RegDstIn,
  input  RegWrEnIn,
  input  [31:0] ALU_RES,
  input  [4:0] WrIdxIn,
  input  [31:0] PCIN,
  input  SyscalIN,
  input  JRIN,
  input  Freeze,
  output [31:0] CacheReadOut,
  output MemToRegOut,
  output JumpOut,
  output RegDstOut,
  output RegWrEnOut,
  output [31:0] AluRes_WB,
  output [4:0] WrIdxOut,
  output [31:0] PCOUT,
  output SyscallOut,
  output JROUT
);

  wire xor_1_out;

  xor xor_1 (xor_1_out, 1'b1, Freeze);
  Register #(.width(32)) register_1 (.D(CacheReadDataIn), .en(xor_1_out), .clk(Clock), .Q(CacheReadOut));  // open: clr
  Register #(.width(1)) register_2 (.D(MemToRegIn), .en(xor_1_out), .clk(Clock), .Q(MemToRegOut));  // open: clr
  Register #(.width(1)) register_3 (.D(JumpIn), .en(xor_1_out), .clk(Clock), .Q(JumpOut));  // open: clr
  Register #(.width(1)) register_4 (.D(RegDstIn), .en(xor_1_out), .clk(Clock), .Q(RegDstOut));  // open: clr
  Register #(.width(1)) register_5 (.D(RegWrEnIn), .en(xor_1_out), .clk(Clock), .Q(RegWrEnOut));  // open: clr
  Register #(.width(32)) register_6 (.D(ALU_RES), .en(xor_1_out), .clk(Clock), .Q(AluRes_WB));  // open: clr
  Register #(.width(5)) register_7 (.D(WrIdxIn), .en(xor_1_out), .clk(Clock), .Q(WrIdxOut));  // open: clr
  Register #(.width(32)) register_8 (.D(PCIN), .en(xor_1_out), .clk(Clock), .Q(PCOUT));  // open: clr
  Register #(.width(1)) register_9 (.D(SyscalIN), .en(xor_1_out), .clk(Clock), .Q(SyscallOut));  // open: clr
  Register #(.width(1)) register_10 (.D(JRIN), .en(xor_1_out), .clk(Clock), .Q(JROUT));  // open: clr
endmodule
