// Logisim project alu.circ as structural Verilog: 1 circuit, main circuit ALU
module ALU (
  input  [31:0] ReadData1,
  input  [31:0] ReadData2,
  input  [4:0] ControlBits,
  output [31:0] Result,
  output Zero
);

  wire comparator_1_lt, comparator_2_eq, comparator_2_lt, comparator_3_eq, comparator_3_gt, comparator_4_eq,
       comparator_5_gt, comparator_6_eq, nor_4_out, nor_5_out, nor_6_out, nor_7_out, nor_8_out, not_1_out,
       or_2_out, or_3_out;
  wire [4:0] xor_1_out, xor_2_out, xor_4_out, xor_5_out, xor_6_out, xor_7_out, xor_8_out;
  wire [31:0] I0, I1, I2, I3, I4, I7, I8, I9, I10, I11, I12, I13, I14, I15, I16, I17, I18, I25, undriven;

  Shifter #(.width(32)) shifter_1 (.in(ReadData2), .\dist (ReadData1[4:0]), .out(I0));
  Shifter #(.shift("lr"), .width(32)) shifter_2 (.in(ReadData2), .\dist (ReadData1[4:0]), .out(I1));
  Shifter #(.shift("ar"), .width(32)) shifter_3 (.in(ReadData2), .\dist (ReadData1[4:0]), .out(I2));
  Shifter #(.width(32)) shifter_4 (.in(ReadData2), .\dist (ReadData1[4:0]), .out(I3));
  Shifter #(.shift("lr"), .width(32)) shifter_5 (.in(ReadData2), .\dist (ReadData1[4:0]), .out(I4));
  assign xor_1_out = ControlBits ^ 5'b00101;  // XOR_Gate xor_1, 5 bits wide
  assign xor_2_out = ControlBits ^ 5'b00110;  // XOR_Gate xor_2, 5 bits wide
  Multiplier #(.mode("twosComplement"), .width(32)) multiplier_1 (
    .a(ReadData1), .b(ReadData2), .out(I7));  // open: cin, cout
  Divider #(.mode("twosComplement"), .width(32)) divider_1 (
    .a(ReadData1), .b(ReadData2), .out(I8));  // open: upper, rem
  Adder #(.width(32)) adder_1 (.a(ReadData1), .b(ReadData2), .out(I9));  // open: cin, cout
  Adder #(.width(32)) adder_2 (.a(ReadData1), .b(ReadData2), .out(I10));  // open: cin, cout
  Subtractor #(.width(32)) subtractor_1 (.a(ReadData1), .b(ReadData2), .out(I11));  // open: bin, bout
  Subtractor #(.width(32)) subtractor_2 (.a(ReadData1), .b(ReadData2), .out(I12));  // open: bin, bout
  assign I13 = ReadData1 & ReadData2;  // AND_Gate and_1, 32 bits wide
  assign I14 = ReadData1 | ReadData2;  // OR_Gate or_1, 32 bits wide
  assign I15 = ReadData1 ^ ReadData2;  // XOR_Gate xor_3, 32 bits wide
  nor nor_1 (Zero, xor_1_out[0], xor_1_out[1], xor_1_out[2], xor_1_out[3], xor_1_out[4]);
  nor nor_2 (Zero, xor_2_out[0], xor_2_out[1], xor_2_out[2], xor_2_out[3], xor_2_out[4]);
  assign I16 = ~(ReadData1 | ReadData2);  // NOR_Gate nor_3, 32 bits wide
  Comparator #(.width(32)) comparator_1 (.a(ReadData1), .b(ReadData2), .lt(comparator_1_lt));  // open: gt, eq
  Adder #(.width(32)) adder_3 (.a(ReadData1), .b(ReadData2), .out(I18));  // open: cin, cout
  Comparator #(.width(32)) comparator_2 (
    .a(ReadData1), .b(ReadData2), .eq(comparator_2_eq), .lt(comparator_2_lt));  // open: gt
  Comparator #(.width(32)) comparator_3 (
    .a(ReadData1), .b(ReadData2), .gt(comparator_3_gt), .eq(comparator_3_eq));  // open: lt
  assign I17 = {{31{1'b0}}, comparator_1_lt};  // Bit_Extender bit_extender_1
  assign xor_4_out = ControlBits ^ 5'b10100;  // XOR_Gate xor_4, 5 bits wide
  assign xor_5_out = ControlBits ^ 5'b10101;  // XOR_Gate xor_5, 5 bits wide
  Comparator #(.width(32)) comparator_4 (.a(ReadData1), .b(ReadData2), .eq(comparator_4_eq));  // open: gt, lt
  assign xor_6_out = ControlBits ^ 5'b10110;  // XOR_Gate xor_6, 5 bits wide
  assign xor_7_out = ControlBits ^ 5'b10111;  // XOR_Gate xor_7, 5 bits wide
  Comparator #(.width(32)) comparator_5 (.a(ReadData1), .b(ReadData2), .gt(comparator_5_gt));  // open: eq, lt
  assign xor_8_out = ControlBits ^ 5'b11000;  // XOR_Gate xor_8, 5 bits wide
  Shifter #(.width(32)) shifter_6 (.in(ReadData2), .\dist (5'b10000), .out(I25));
  nor nor_4 (nor_4_out, xor_4_out[0], xor_4_out[1], xor_4_out[2], xor_4_out[3], xor_4_out[4]);
  Comparator #(.width(32)) comparator_6 (.a(ReadData1), .b(ReadData2), .eq(comparator_6_eq));  // open: gt, lt
  nor nor_5 (nor_5_out, xor_5_out[0], xor_5_out[1], xor_5_out[2], xor_5_out[3], xor_5_out[4]);
  not not_1 (not_1_out, comparator_4_eq);
  nor nor_6 (nor_6_out, xor_6_out[0], xor_6_out[1], xor_6_out[2], xor_6_out[3], xor_6_out[4]);
  or or_2 (or_2_out, comparator_2_eq, comparator_2_lt);
  nor nor_7 (nor_7_out, xor_7_out[0], xor_7_out[1], xor_7_out[2], xor_7_out[3], xor_7_out[4]);
  nor nor_8 (nor_8_out, xor_8_out[0], xor_8_out[1], xor_8_out[2], xor_8_out[3], xor_8_out[4]);
  or or_3 (or_3_out, comparator_3_gt, comparator_3_eq);
  and and_2 (Zero, nor_4_out, comparator_6_eq);
  and and_3 (Zero, nor_5_out, not_1_out);
  and and_4 (Zero, nor_6_out, or_2_out);
  and and_5 (Zero, nor_7_out, comparator_5_gt);
  and and_6 (Zero, nor_8_out, or_3_out);
  Multiplexer #(.enable("true"), .select(5), .width(32)) multiplexer_1 (
    .in0(I0), .in1(I1), .in2(I2), .in3(I3), .in4(I4), .in5(ReadData1), .in6({32{1'b1}}), .in7(I7), .in8(I8),
    .in9(I9), .in10(I10), .in11(I11), .in12(I12), .in13(I13), .in14(I14), .in15(I15), .in16(I16), .in17(I17),
    .in18(I18), .in19(I18), .in25(I25), .in31(undriven), .out(Result), .sel(ControlBits));  // open: in20, in21, in22, in23, in24, in26, in27, in28, in29, in30, en

  // Other names for the same wires on the sheet: I5[31:0] = ReadData1; I19[31:0] = I18

  // Notes on the sheet:
  //   use an AND gate after adding the other types!
  //   syscall
  //   signed?
  //   unsigned?
endmodule
