// Logisim project branchDetector.circ as structural Verilog: 1 circuit, main circuit branch_detector
module branch_detector (
  input  clk,
  input  rst,
  input  [31:0] command,
  input  [31:0] pc,
  input  Frz,
  output [31:0] pc_branch,
  output Branch,
  output [31:0] pc_branch_delayed,
  output Jump,
  output [31:0] pc_4_delayed
);

  wire and_1_out, and_2_out, I0_N, I1_N, I2_N, I3_N, I4_N, I5_N, xor_1_out;
  wire [31:0] adder_2_out, bit_extender_1_out, register_1_q, register_2_q, register_3_q, shifter_1_out;

  and and_1 (and_1_out, command[26], I1_N, I3_N);
  and and_2 (and_2_out, I3_N, command[28]);
  and and_3 (Jump, I5_N, I3_N, I2_N, command[27]);
  or or_1 (Branch, and_1_out, and_2_out);
  not not_1 (I5_N, command[31]);
  not not_2 (I4_N, command[30]);
  not not_3 (I3_N, command[29]);
  not not_4 (I2_N, command[28]);
  not not_5 (I1_N, command[27]);
  not not_6 (I0_N, command[26]);
  xor xor_1 (xor_1_out, Frz, 1'b1);
  assign bit_extender_1_out = {{16{command[15]}}, command[15:0]};  // Bit_Extender bit_extender_1
  Register #(.width(32)) register_1 (.D(pc), .en(xor_1_out), .clk(clk), .Q(register_1_q));  // open: clr
  Shifter #(.width(32)) shifter_1 (.in(bit_extender_1_out), .\dist (5'b00010), .out(shifter_1_out));
  Adder #(.width(32)) adder_1 (.a(shifter_1_out), .b(register_1_q), .out(pc_branch));  // open: cin, cout
  Adder #(.width(32)) adder_2 (.a(register_1_q), .b(32'h4), .out(adder_2_out));  // open: cin, cout
  Register #(.width(32)) register_2 (.D(pc_branch), .en(xor_1_out), .clk(clk), .Q(register_2_q), .clr(rst));
  Register #(.width(32)) register_3 (.D(adder_2_out), .en(xor_1_out), .clk(clk), .Q(register_3_q), .clr(rst));
  Register #(.width(32)) register_4 (.D(register_2_q), .en(xor_1_out), .clk(clk), .Q(pc_branch_delayed), .clr(rst));
  Register #(.width(32)) register_5 (.D(register_3_q), .en(xor_1_out), .clk(clk), .Q(pc_4_delayed), .clr(rst));

  // Other names for the same wires on the sheet: I0 = command[26]; Opcode[5:0] = command[31:26]; I1 = command[27];
  //   I2 = command[28]; I3 = command[29]; I4 = command[30]; I5 = command[31]
endmodule
