// Logisim project branch_predictor.circ as structural Verilog: 1 circuit, main circuit branchPredictor
module branchPredictor (
  input  Jump,
  input  Branch,
  input  Clock,
  input  Zero,
  input  rst_cnt,
  input  Frz,
  output Prediction,
  output wrongPrediction,
  output pcBranch,
  output reset
);

  wire and_1_out, and_2_out, and_3_out, and_4_out, and_5_out, and_6_out, and_7_out, and_8_out,
       comparator_1_gt, counter_1_carry, delayedBranch, delayedPrediction, Frz_t, not_1_out, or_1_out,
       or_2_out, Q1, Q2, register_3_q, register_5_q, xor_2_out;

  xor xor_1 (Frz_t, Frz, 1'b1);
  and and_1 (and_1_out, Branch, Frz_t);
  Counter #(.max('h1), .width(1)) counter_1 (
    .clr(rst_cnt), .load(1'b0), .up(1'b1), .count(and_1_out), .clk(Clock), .carry(counter_1_carry));  // open: D, Q
  not not_1 (not_1_out, Q1);
  and and_2 (and_2_out, Q2, Zero);
  and and_3 (and_3_out, Zero, not_1_out);
  or or_1 (or_1_out, and_2_out, and_3_out, and_4_out);
  and and_4 (and_4_out, not_1_out, Q2);
  and and_5 (and_5_out, Q2, Q1);
  and and_6 (and_6_out, Q1, Zero);
  or or_2 (or_2_out, and_5_out, and_6_out, and_7_out);
  and and_7 (and_7_out, Q2, Zero);
  and and_8 (and_8_out, counter_1_carry, Frz_t);
  Register #(.width(1)) register_1 (.D(or_1_out), .en(and_8_out), .clk(Clock), .Q(Q1));  // open: clr
  Register #(.width(1)) register_2 (.D(or_2_out), .en(and_8_out), .clk(Clock), .Q(Q2));  // open: clr
  xor xor_2 (xor_2_out, delayedPrediction, Zero);
  and and_9 (wrongPrediction, delayedBranch, xor_2_out);
  Comparator #(.mode("unsigned"), .width(2)) comparator_1 (
    .a({Q2, Q1}), .b(2'b01), .gt(comparator_1_gt));  // open: eq, lt
  Multiplexer multiplexer_1 (.in0(1'b0), .in1(comparator_1_gt), .out(Prediction), .sel(Branch));
  Register #(.width(1)) register_3 (.D(Branch), .en(Frz_t), .clk(Clock), .Q(register_3_q));  // open: clr
  Register #(.width(1)) register_4 (.D(register_3_q), .en(Frz_t), .clk(Clock), .Q(delayedBranch));  // open: clr
  Register #(.width(1)) register_5 (.D(Prediction), .en(Frz_t), .clk(Clock), .Q(register_5_q));  // open: clr
  Register #(.width(1)) register_6 (.D(wrongPrediction), .en(Frz_t), .clk(Clock), .Q(reset));  // open: clr
  Register #(.width(1)) register_7 (.D(register_5_q), .en(Frz_t), .clk(Clock), .Q(delayedPrediction));  // open: clr

  assign pcBranch = Zero;
endmodule
