// Logisim project cache.circ as structural Verilog: 1 circuit, main circuit Cache
module Cache (
  input  clk,
  input  [31:0] Address,
  input  WriteEnable,
  input  [31:0] WriteData,
  input  CacheAccess,
  output ReadFromMem,
  output [31:0] ReadData,
  output HIT,
  output [31:0] AddressOut,
  output WriteInMemory,
  output Last_WE,
  output [31:0] WriteDataOut,
  output [31:0] Last_W_Data,
  output [31:0] RFMAddress,
  output WE_select
);

  wire and_9_out, and_10_out, and_11_out, and_12_out, and_13_out, and_14_out, and_15_out, and_16_out,
       and_50_out, and_51_out, and_52_out, and_53_out, and_54_out, and_55_out, and_56_out, and_57_out,
       and_67_out, and_68_out, and_69_out, and_70_out, and_71_out, and_72_out, and_73_out, and_74_out, C0,
       C1, C2, C3, comparator_2_eq, comparator_4_eq, comparator_6_eq, comparator_8_eq, d_ff_1_q, d_ff_2_q,
       d_ff_3_q, d_ff_4_q, d_ff_5_q, d_ff_6_q, d_ff_7_q, d_ff_8_q, d_ff_9_q, d_ff_10_q, d_ff_11_q, d_ff_12_q,
       d_ff_13_q, d_ff_14_q, d_ff_15_q, d_ff_16_q, d_ff_17_q, d_ff_18_q, d_ff_19_q, d_ff_20_q, d_ff_21_q,
       d_ff_22_q, d_ff_23_q, d_ff_24_q, d_ff_25_q, d_ff_26_q, d_ff_27_q, d_ff_28_q, d_ff_29_q, d_ff_30_q,
       d_ff_31_q, d_ff_32_q, d_ff_33_q, d_ff_34_q, d_ff_35_q, d_ff_36_q, d_ff_37_q, d_ff_38_q, DC0, DC1, DC2,
       DC3, multiplexer_19_out, not_1_out, not_2_out, not_3_out, not_4_out, not_5_out, not_6_out, not_7_out,
       not_8_out, not_9_out, not_10_out, not_11_out, not_12_out, not_13_out, not_14_out, not_15_out,
       not_16_out, not_17_out, not_18_out, not_19_out, not_20_out, not_21_out, not_22_out, not_23_out,
       not_24_out, not_25_out, not_26_out, not_27_out, not_28_out, not_29_out, not_30_out, not_31_out,
       not_32_out, not_33_out, not_34_out, not_35_out, not_36_out, not_37_out, not_38_out, not_39_out,
       not_40_out, not_41_out, not_42_out, not_43_out, not_44_out, not_45_out, not_46_out, not_47_out,
       not_48_out, or_1_out, or_2_out, or_3_out, or_4_out, or_5_out, or_7_out, or_9_out, Select_0, Select_1,
       Select_2, Select_3, Set0, Set1, Set2, Set3, SetAddressOut, TE0, TE1, TE2, TE3, TE4, TE5, TE6, TE7,
       Tmp_En, Tmp_writeEnable, V0, V1, V2, V3, V4, V5, V6, V7, VE0, VE1, VE2, VE3, VE4, VE5, VE6, VE7, WE0,
       WE1, WE2, WE3, WE4, WE5, WE6, WE7, WE8, WE9, WE10, WE11, WE12, WE13, WE14, WE15, WE16, WE17, WE18,
       WE19, WE20, WE21, WE22, WE23, WE24, WE25, WE26, WE27, WE28, WE29, WE30, WE31, WH, Word0, Word1, Word2,
       Word3;
  wire [0:0] multiplexer_20_out;
  wire [1:0] adder_1_out, adder_5_out, adder_6_out, register_53_q, register_54_q, register_55_q;
  wire [9:0] multiplexer_25_out, T0, T1, T2, T3, T4, T5, T6, T7;
  wire [31:0] adder_2_out, adder_3_out, adder_4_out, and_75_out, fiveclockdelay_1_dataout, multiplexer_6_out,
       multiplexer_7_out, multiplexer_8_out, multiplexer_9_out, multiplexer_10_out, multiplexer_11_out,
       multiplexer_12_out, multiplexer_13_out, multiplexer_14_out, multiplexer_15_out, multiplexer_16_out,
       multiplexer_17_out, multiplexer_21_out, multiplexer_22_out, multiplexer_23_out, multiplexer_24_out,
       multiplexer_26_out, register_56_q, register_57_q, register_58_q, register_59_q, W0, W1, W2, W3, W4,
       W5, W6, W7, W8, W9, W10, W11, W12, W13, W14, W15, W16, W17, W18, W19, W20, W21, W22, W23, W24, W25,
       W26, W27, W28, W29, W30, W31;

  Decoder #(.select(2)) decoder_1 (.out0(Set0), .out1(Set1), .out2(Set2), .out3(Set3), .sel(Address[5:4]));  // open: en
  Decoder #(.select(2)) decoder_2 (
    .out0(Word0), .out1(Word1), .out2(Word2), .out3(Word3), .sel(Address[3:2]));  // open: en
  not not_1 (not_1_out, C0);
  not not_2 (not_2_out, C1);
  not not_3 (not_3_out, C2);
  not not_4 (not_4_out, C3);
  not not_5 (not_5_out, HIT);
  not not_6 (not_6_out, HIT);
  not not_7 (not_7_out, HIT);
  not not_8 (not_8_out, HIT);
  not not_9 (not_9_out, HIT);
  not not_10 (not_10_out, HIT);
  not not_11 (not_11_out, HIT);
  not not_12 (not_12_out, HIT);
  and and_1 (TE0, Set0, C0, not_5_out);
  and and_2 (TE1, Set0, not_1_out, not_6_out);
  and and_3 (TE2, Set1, C1, not_7_out);
  and and_4 (TE3, Set1, not_2_out, not_8_out);
  and and_5 (TE4, Set2, C2, not_9_out);
  and and_6 (TE5, Set2, not_3_out, not_10_out);
  and and_7 (TE6, Set3, C3, not_11_out);
  and and_8 (TE7, Set3, not_4_out, not_12_out);
  and and_9 (and_9_out, ~Select_0, Set0, WH);  // AND_Gate
  and and_10 (and_10_out, Select_0, Set0, WH);
  and and_11 (and_11_out, ~Select_1, Set1, WH);  // AND_Gate
  and and_12 (and_12_out, Select_1, Set1, WH);
  and and_13 (and_13_out, ~Select_2, Set2, WH);  // AND_Gate
  and and_14 (and_14_out, Select_2, Set2, WH);
  and and_15 (and_15_out, ~Select_3, Set3, WH);  // AND_Gate
  and and_16 (and_16_out, Select_3, Set3, WH);
  and and_17 (WH, WriteEnable, HIT);
  and and_18 (WE0, Word0, and_9_out);
  and and_19 (WE4, Word0, and_10_out);
  and and_20 (WE8, Word0, and_11_out);
  and and_21 (WE12, Word0, and_12_out);
  and and_22 (WE16, Word0, and_13_out);
  and and_23 (WE20, Word0, and_14_out);
  and and_24 (WE24, Word0, and_15_out);
  and and_25 (WE28, Word0, and_16_out);
  and and_26 (WE1, Word1, and_9_out);
  and and_27 (WE5, Word1, and_10_out);
  and and_28 (WE9, Word1, and_11_out);
  and and_29 (WE13, Word1, and_12_out);
  and and_30 (WE17, Word1, and_13_out);
  and and_31 (WE21, Word1, and_14_out);
  and and_32 (WE25, Word1, and_15_out);
  and and_33 (WE29, Word1, and_16_out);
  and and_34 (WE2, Word2, and_9_out);
  and and_35 (WE6, Word2, and_10_out);
  and and_36 (WE10, Word2, and_11_out);
  and and_37 (WE14, Word2, and_12_out);
  and and_38 (WE18, Word2, and_13_out);
  and and_39 (WE22, Word2, and_14_out);
  and and_40 (WE26, Word2, and_15_out);
  and and_41 (WE30, Word2, and_16_out);
  and and_42 (WE3, Word3, and_9_out);
  and and_43 (WE7, Word3, and_10_out);
  and and_44 (WE11, Word3, and_11_out);
  and and_45 (WE15, Word3, and_12_out);
  and and_46 (WE19, Word3, and_13_out);
  and and_47 (WE23, Word3, and_14_out);
  and and_48 (WE27, Word3, and_15_out);
  and and_49 (WE31, Word3, and_16_out);
  Comparator #(.width(10)) comparator_1 (.a(T1), .b(Address[15:6]), .eq(Select_0));  // open: gt, lt
  Comparator #(.width(10)) comparator_2 (.a(T0), .b(Address[15:6]), .eq(comparator_2_eq));  // open: gt, lt
  and and_50 (and_50_out, V1, Select_0);
  and and_51 (and_51_out, V0, comparator_2_eq);
  or or_1 (or_1_out, and_50_out, and_51_out);
  Comparator #(.width(10)) comparator_3 (.a(T3), .b(Address[15:6]), .eq(Select_1));  // open: gt, lt
  Comparator #(.width(10)) comparator_4 (.a(T2), .b(Address[15:6]), .eq(comparator_4_eq));  // open: gt, lt
  and and_52 (and_52_out, V3, Select_1);
  and and_53 (and_53_out, V2, comparator_4_eq);
  Multiplexer #(.select(2)) multiplexer_1 (
    .in0(or_1_out), .in1(or_2_out), .in2(or_3_out), .in3(or_4_out), .out(HIT), .sel(Address[5:4]));
  or or_2 (or_2_out, and_52_out, and_53_out);
  Register #(.width(1)) register_1 (.D(DC1), .en(Set1), .clk(clk), .Q(C1));  // open: clr
  Register #(.width(1)) register_2 (.D(DC2), .en(Set2), .clk(clk), .Q(C2));  // open: clr
  Register #(.width(1)) register_3 (.D(DC3), .en(Set3), .clk(clk), .Q(C3));  // open: clr
  Comparator #(.width(10)) comparator_5 (.a(T5), .b(Address[15:6]), .eq(Select_2));  // open: gt, lt
  Comparator #(.width(10)) comparator_6 (.a(T4), .b(Address[15:6]), .eq(comparator_6_eq));  // open: gt, lt
  Register #(.width(1)) register_4 (.D(DC0), .en(Set0), .clk(clk), .Q(C0));  // open: clr
  and and_54 (and_54_out, V5, Select_2);
  or or_3 (or_3_out, and_54_out, and_55_out);
  and and_55 (and_55_out, V4, comparator_6_eq);
  Register #(.width(1)) register_5 (.D(1'b1), .en(VE0), .clk(clk), .Q(V0));  // open: clr
  Register #(.width(1)) register_6 (.D(1'b1), .en(VE1), .clk(clk), .Q(V1));  // open: clr
  Register #(.width(1)) register_7 (.D(1'b1), .en(VE2), .clk(clk), .Q(V2));  // open: clr
  Register #(.width(1)) register_8 (.D(1'b1), .en(VE3), .clk(clk), .Q(V3));  // open: clr
  Register #(.width(1)) register_9 (.D(1'b1), .en(VE4), .clk(clk), .Q(V4));  // open: clr
  Register #(.width(1)) register_10 (.D(1'b1), .en(VE5), .clk(clk), .Q(V5));  // open: clr
  Register #(.width(1)) register_11 (.D(1'b1), .en(VE6), .clk(clk), .Q(V6));  // open: clr
  Register #(.width(1)) register_12 (.D(1'b1), .en(VE7), .clk(clk), .Q(V7));  // open: clr
  Comparator #(.width(10)) comparator_7 (.a(T7), .b(Address[15:6]), .eq(Select_3));  // open: gt, lt
  Comparator #(.width(10)) comparator_8 (.a(T6), .b(Address[15:6]), .eq(comparator_8_eq));  // open: gt, lt
  and and_56 (and_56_out, V7, Select_3);
  and and_57 (and_57_out, V6, comparator_8_eq);
  Register #(.width(10)) register_13 (.D(Address[15:6]), .en(TE0), .clk(clk), .Q(T0));  // open: clr
  Register #(.width(10)) register_14 (.D(Address[15:6]), .en(TE1), .clk(clk), .Q(T1));  // open: clr
  Register #(.width(10)) register_15 (.D(Address[15:6]), .en(TE2), .clk(clk), .Q(T2));  // open: clr
  Register #(.width(10)) register_16 (.D(Address[15:6]), .en(TE3), .clk(clk), .Q(T3));  // open: clr
  Register #(.width(10)) register_17 (.D(Address[15:6]), .en(TE4), .clk(clk), .Q(T4));  // open: clr
  Register #(.width(10)) register_18 (.D(Address[15:6]), .en(TE5), .clk(clk), .Q(T5));  // open: clr
  Register #(.width(10)) register_19 (.D(Address[15:6]), .en(TE6), .clk(clk), .Q(T6));  // open: clr
  Register #(.width(10)) register_20 (.D(Address[15:6]), .en(TE7), .clk(clk), .Q(T7));  // open: clr
  or or_4 (or_4_out, and_56_out, and_57_out);
  Register #(.width(32)) register_21 (.D(WriteData), .en(WE0), .clk(clk), .Q(W0));  // open: clr
  Register #(.width(32)) register_22 (.D(WriteData), .en(WE4), .clk(clk), .Q(W4));  // open: clr
  Register #(.width(32)) register_23 (.D(WriteData), .en(WE8), .clk(clk), .Q(W8));  // open: clr
  Register #(.width(32)) register_24 (.D(WriteData), .en(WE12), .clk(clk), .Q(W12));  // open: clr
  Register #(.width(32)) register_25 (.D(WriteData), .en(WE16), .clk(clk), .Q(W16));  // open: clr
  Register #(.width(32)) register_26 (.D(WriteData), .en(WE20), .clk(clk), .Q(W20));  // open: clr
  Register #(.width(32)) register_27 (.D(WriteData), .en(WE24), .clk(clk), .Q(W24));  // open: clr
  Register #(.width(32)) register_28 (.D(WriteData), .en(WE28), .clk(clk), .Q(W28));  // open: clr
  Register #(.width(32)) register_29 (.D(WriteData), .en(WE1), .clk(clk), .Q(W1));  // open: clr
  Register #(.width(32)) register_30 (.D(WriteData), .en(WE5), .clk(clk), .Q(W5));  // open: clr
  Register #(.width(32)) register_31 (.D(WriteData), .en(WE9), .clk(clk), .Q(W9));  // open: clr
  Register #(.width(32)) register_32 (.D(WriteData), .en(WE13), .clk(clk), .Q(W13));  // open: clr
  Register #(.width(32)) register_33 (.D(WriteData), .en(WE17), .clk(clk), .Q(W17));  // open: clr
  Register #(.width(32)) register_34 (.D(WriteData), .en(WE21), .clk(clk), .Q(W21));  // open: clr
  Register #(.width(32)) register_35 (.D(WriteData), .en(WE25), .clk(clk), .Q(W25));  // open: clr
  Register #(.width(32)) register_36 (.D(WriteData), .en(WE29), .clk(clk), .Q(W29));  // open: clr
  not not_13 (not_13_out, C0);
  not not_14 (not_14_out, C1);
  not not_15 (not_15_out, C2);
  not not_16 (not_16_out, C3);
  Multiplexer multiplexer_2 (.in0(not_13_out), .in1(Select_0), .out(DC0), .sel(HIT));
  Multiplexer multiplexer_3 (.in0(not_14_out), .in1(Select_1), .out(DC1), .sel(HIT));
  Multiplexer multiplexer_4 (.in0(not_15_out), .in1(Select_2), .out(DC2), .sel(HIT));
  Multiplexer multiplexer_5 (.in0(not_16_out), .in1(Select_3), .out(DC3), .sel(HIT));
  Register #(.width(32)) register_37 (.D(WriteData), .en(WE2), .clk(clk), .Q(W2));  // open: clr
  Register #(.width(32)) register_38 (.D(WriteData), .en(WE6), .clk(clk), .Q(W6));  // open: clr
  Register #(.width(32)) register_39 (.D(WriteData), .en(WE10), .clk(clk), .Q(W10));  // open: clr
  Register #(.width(32)) register_40 (.D(WriteData), .en(WE14), .clk(clk), .Q(W14));  // open: clr
  Register #(.width(32)) register_41 (.D(WriteData), .en(WE18), .clk(clk), .Q(W18));  // open: clr
  Register #(.width(32)) register_42 (.D(WriteData), .en(WE22), .clk(clk), .Q(W22));  // open: clr
  Register #(.width(32)) register_43 (.D(WriteData), .en(WE26), .clk(clk), .Q(W26));  // open: clr
  Register #(.width(32)) register_44 (.D(WriteData), .en(WE30), .clk(clk), .Q(W30));  // open: clr
  Register #(.width(32)) register_45 (.D(WriteData), .en(WE3), .clk(clk), .Q(W3));  // open: clr
  Register #(.width(32)) register_46 (.D(WriteData), .en(WE7), .clk(clk), .Q(W7));  // open: clr
  Register #(.width(32)) register_47 (.D(WriteData), .en(WE11), .clk(clk), .Q(W11));  // open: clr
  Register #(.width(32)) register_48 (.D(WriteData), .en(WE15), .clk(clk), .Q(W15));  // open: clr
  Register #(.width(32)) register_49 (.D(WriteData), .en(WE19), .clk(clk), .Q(W19));  // open: clr
  Register #(.width(32)) register_50 (.D(WriteData), .en(WE23), .clk(clk), .Q(W23));  // open: clr
  Register #(.width(32)) register_51 (.D(WriteData), .en(WE27), .clk(clk), .Q(W27));  // open: clr
  Register #(.width(32)) register_52 (.D(WriteData), .en(WE31), .clk(clk), .Q(W31));  // open: clr
  Multiplexer #(.select(2), .width(32)) multiplexer_6 (
    .in0(W8), .in1(W9), .in2(W10), .in3(W11), .out(multiplexer_6_out), .sel(Address[3:2]));
  Multiplexer #(.select(2), .width(32)) multiplexer_7 (
    .in0(W12), .in1(W13), .in2(W14), .in3(W15), .out(multiplexer_7_out), .sel(Address[3:2]));
  Multiplexer #(.select(2), .width(32)) multiplexer_8 (
    .in0(W16), .in1(W17), .in2(W18), .in3(W19), .out(multiplexer_8_out), .sel(Address[3:2]));
  Multiplexer #(.select(2), .width(32)) multiplexer_9 (
    .in0(W20), .in1(W21), .in2(W22), .in3(W23), .out(multiplexer_9_out), .sel(Address[3:2]));
  Multiplexer #(.select(2), .width(32)) multiplexer_10 (
    .in0(W24), .in1(W25), .in2(W26), .in3(W27), .out(multiplexer_10_out), .sel(Address[3:2]));
  Multiplexer #(.select(2), .width(32)) multiplexer_11 (
    .in0(W28), .in1(W29), .in2(W30), .in3(W31), .out(multiplexer_11_out), .sel(Address[3:2]));
  Multiplexer #(.select(2), .width(32)) multiplexer_12 (
    .in0(W0), .in1(W1), .in2(W2), .in3(W3), .out(multiplexer_12_out), .sel(Address[3:2]));
  Multiplexer #(.select(2), .width(32)) multiplexer_13 (
    .in0(W4), .in1(W5), .in2(W6), .in3(W7), .out(multiplexer_13_out), .sel(Address[3:2]));
  not not_17 (not_17_out, HIT);
  not not_18 (not_18_out, V0);
  not not_19 (not_19_out, C0);
  not not_20 (not_20_out, HIT);
  not not_21 (not_21_out, V1);
  not not_22 (not_22_out, HIT);
  not not_23 (not_23_out, V2);
  not not_24 (not_24_out, C1);
  not not_25 (not_25_out, HIT);
  not not_26 (not_26_out, V3);
  Multiplexer #(.width(32)) multiplexer_14 (
    .in0(multiplexer_12_out), .in1(multiplexer_13_out), .out(multiplexer_14_out), .sel(Select_0));
  Multiplexer #(.width(32)) multiplexer_15 (
    .in0(multiplexer_6_out), .in1(multiplexer_7_out), .out(multiplexer_15_out), .sel(Select_1));
  Multiplexer #(.width(32)) multiplexer_16 (
    .in0(multiplexer_8_out), .in1(multiplexer_9_out), .out(multiplexer_16_out), .sel(Select_2));
  Multiplexer #(.width(32)) multiplexer_17 (
    .in0(multiplexer_10_out), .in1(multiplexer_11_out), .out(multiplexer_17_out), .sel(Select_3));
  and and_58 (VE0, C0, not_17_out, Set0, not_18_out);
  and and_59 (VE1, not_19_out, not_20_out, Set0, not_21_out);
  and and_60 (VE2, C1, not_22_out, Set1, not_23_out);
  and and_61 (VE3, not_24_out, not_25_out, Set1, not_26_out);
  Multiplexer #(.select(2), .width(32)) multiplexer_18 (
    .in0(multiplexer_14_out), .in1(multiplexer_15_out), .in2(multiplexer_16_out), .in3(multiplexer_17_out),
    .out(ReadData), .sel(Address[5:4]));
  not not_27 (not_27_out, HIT);
  not not_28 (not_28_out, V4);
  not not_29 (not_29_out, C2);
  not not_30 (not_30_out, HIT);
  not not_31 (not_31_out, V5);
  not not_32 (not_32_out, HIT);
  not not_33 (not_33_out, V6);
  not not_34 (not_34_out, C3);
  not not_35 (not_35_out, HIT);
  not not_36 (not_36_out, V7);
  and and_62 (VE4, C2, not_27_out, Set2, not_28_out);
  and and_63 (VE5, not_29_out, not_30_out, Set2, not_31_out);
  and and_64 (VE6, C3, not_32_out, Set3, not_33_out);
  and and_65 (VE7, not_34_out, not_35_out, Set3, not_36_out);
  not not_37 (not_37_out, C0);
  not not_38 (not_38_out, C1);
  not not_39 (not_39_out, C2);
  not not_40 (not_40_out, C3);
  Multiplexer #(.select(3)) multiplexer_19 (
    .in0(V0), .in1(V1), .in2(V2), .in3(V3), .in4(V4), .in5(V5), .in6(V6), .in7(V7), .out(multiplexer_19_out),
    .sel({Address[5:4], multiplexer_20_out[0]}));
  not not_41 (not_41_out, HIT);
  Multiplexer #(.select(2)) multiplexer_20 (
    .in0(not_37_out), .in1(not_38_out), .in2(not_39_out), .in3(not_40_out), .out(multiplexer_20_out[0]),
    .sel(Address[5:4]));
  and and_66 (Tmp_En, multiplexer_19_out, and_67_out);
  and and_67 (and_67_out, CacheAccess, not_41_out);
  not not_42 (not_42_out, HIT);
  and and_68 (and_68_out, CacheAccess, not_42_out);
  D_Flip_Flop d_ff_1 (.D(and_68_out), .clk(clk), .Q(d_ff_1_q));  // open: Qn, preset, reset
  and and_69 (and_69_out, CacheAccess, not_43_out);
  not not_43 (not_43_out, HIT);
  D_Flip_Flop d_ff_2 (.D(d_ff_1_q), .clk(clk), .Q(d_ff_2_q));  // open: Qn, preset, reset
  not not_44 (not_44_out, HIT);
  Multiplexer #(.select(3), .width(32)) multiplexer_21 (
    .in0(W0), .in1(W4), .in2(W8), .in3(W12), .in4(W16), .in5(W20), .in6(W24), .in7(W28),
    .out(multiplexer_21_out), .sel({Address[5:4], multiplexer_20_out[0]}));
  Multiplexer #(.select(3), .width(32)) multiplexer_22 (
    .in0(W1), .in1(W5), .in2(W9), .in3(W13), .in4(W17), .in5(W21), .in6(W25), .in7(W29),
    .out(multiplexer_22_out), .sel({Address[5:4], multiplexer_20_out[0]}));
  Multiplexer #(.select(3), .width(32)) multiplexer_23 (
    .in0(W2), .in1(W6), .in2(W10), .in3(W14), .in4(W18), .in5(W22), .in6(W26), .in7(W30),
    .out(multiplexer_23_out), .sel({Address[5:4], multiplexer_20_out[0]}));
  Multiplexer #(.select(3), .width(32)) multiplexer_24 (
    .in0(W3), .in1(W7), .in2(W11), .in3(W15), .in4(W19), .in5(W23), .in6(W27), .in7(W31),
    .out(multiplexer_24_out), .sel({Address[5:4], multiplexer_20_out[0]}));
  Multiplexer #(.select(3), .width(10)) multiplexer_25 (
    .in0(T0), .in1(T1), .in2(T2), .in3(T3), .in4(T4), .in5(T5), .in6(T6), .in7(T7), .out(multiplexer_25_out),
    .sel({Address[5:4], multiplexer_20_out[0]}));
  D_Flip_Flop d_ff_3 (.D(d_ff_2_q), .clk(clk), .Q(d_ff_3_q));  // open: Qn, preset, reset
  not not_45 (not_45_out, HIT);
  D_Flip_Flop d_ff_4 (.D(and_69_out), .clk(clk), .Q(d_ff_4_q));  // open: Qn, preset, reset
  and and_70 (and_70_out, CacheAccess, not_44_out);
  not not_46 (not_46_out, HIT);
  and and_71 (and_71_out, CacheAccess, not_45_out);
  D_Flip_Flop d_ff_5 (.D(d_ff_4_q), .clk(clk), .Q(d_ff_5_q));  // open: Qn, preset, reset
  D_Flip_Flop d_ff_6 (.D(and_70_out), .clk(clk), .Q(d_ff_6_q));  // open: Qn, preset, reset
  Register #(.width(32)) Tmp_writeData (.D(WriteData), .en(and_72_out), .clk(clk), .Q(Last_W_Data));  // open: clr
  and and_72 (and_72_out, CacheAccess, not_46_out);
  D_Flip_Flop d_ff_7 (.D(d_ff_5_q), .clk(clk), .Q(d_ff_7_q));  // open: Qn, preset, reset
  D_Flip_Flop d_ff_8 (.D(d_ff_6_q), .clk(clk), .Q(d_ff_8_q));  // open: Qn, preset, reset
  or or_5 (or_5_out, and_68_out, d_ff_1_q, d_ff_2_q, d_ff_3_q);
  Register #(.width(1)) u_Tmp_writeEnable (
    .D(WriteEnable), .en(and_71_out), .clk(clk), .Q(Tmp_writeEnable));  // open: clr
  D_Flip_Flop d_ff_9 (.D(d_ff_7_q), .clk(clk), .Q(d_ff_9_q));  // open: Qn, preset, reset
  D_Flip_Flop d_ff_10 (.D(d_ff_8_q), .clk(clk), .Q(d_ff_10_q));  // open: Qn, preset, reset
  Register #(.width(2)) register_53 (.D(adder_1_out), .en(or_5_out), .clk(clk), .Q(register_53_q));  // open: clr
  D_Flip_Flop d_ff_11 (.D(d_ff_9_q), .clk(clk), .Q(d_ff_11_q));  // open: Qn, preset, reset
  D_Flip_Flop d_ff_12 (.D(d_ff_10_q), .clk(clk), .Q(d_ff_12_q));  // open: Qn, preset, reset
  and and_73 (and_73_out, CacheAccess, not_47_out);
  not not_47 (not_47_out, HIT);
  D_Flip_Flop d_ff_13 (.D(d_ff_11_q), .clk(clk), .Q(d_ff_13_q));  // open: Qn, preset, reset
  D_Flip_Flop d_ff_14 (.D(d_ff_12_q), .clk(clk), .Q(d_ff_14_q));  // open: Qn, preset, reset
  not not_48 (not_48_out, HIT);
  Adder #(.width(2)) adder_1 (.a(register_53_q), .b(2'b01), .out(adder_1_out));  // open: cin, cout
  D_Flip_Flop d_ff_15 (.D(and_73_out), .clk(clk), .Q(d_ff_15_q));  // open: Qn, preset, reset
  D_Flip_Flop d_ff_16 (.D(d_ff_13_q), .clk(clk), .Q(d_ff_16_q));  // open: Qn, preset, reset
  D_Flip_Flop d_ff_17 (.D(d_ff_14_q), .clk(clk), .Q(d_ff_17_q));  // open: Qn, preset, reset
  and and_74 (and_74_out, CacheAccess, not_48_out);
  D_Flip_Flop d_ff_18 (.D(and_74_out), .clk(clk), .Q(d_ff_18_q));  // open: Qn, preset, reset
  D_Flip_Flop d_ff_19 (.D(Tmp_En), .clk(clk), .Q(d_ff_19_q));  // open: Qn, preset, reset
  D_Flip_Flop d_ff_20 (.D(Tmp_En), .clk(clk), .Q(d_ff_20_q));  // open: Qn, preset, reset
  D_Flip_Flop d_ff_21 (.D(d_ff_15_q), .clk(clk), .Q(d_ff_21_q));  // open: Qn, preset, reset
  D_Flip_Flop d_ff_22 (.D(d_ff_16_q), .clk(clk), .Q(d_ff_22_q));  // open: Qn, preset, reset
  D_Flip_Flop d_ff_23 (.D(d_ff_17_q), .clk(clk), .Q(d_ff_23_q));  // open: Qn, preset, reset
  D_Flip_Flop d_ff_24 (.D(d_ff_18_q), .clk(clk), .Q(d_ff_24_q));  // open: Qn, preset, reset
  D_Flip_Flop d_ff_25 (.D(d_ff_19_q), .clk(clk), .Q(d_ff_25_q));  // open: Qn, preset, reset
  D_Flip_Flop d_ff_26 (.D(d_ff_20_q), .clk(clk), .Q(d_ff_26_q));  // open: Qn, preset, reset
  D_Flip_Flop d_ff_27 (.D(d_ff_21_q), .clk(clk), .Q(d_ff_27_q));  // open: Qn, preset, reset
  D_Flip_Flop d_ff_28 (.D(d_ff_23_q), .clk(clk), .Q(d_ff_28_q));  // open: Qn, preset, reset
  D_Flip_Flop d_ff_29 (.D(d_ff_24_q), .clk(clk), .Q(d_ff_29_q));  // open: Qn, preset, reset
  D_Flip_Flop d_ff_30 (.D(d_ff_25_q), .clk(clk), .Q(d_ff_30_q));  // open: Qn, preset, reset
  D_Flip_Flop d_ff_31 (.D(d_ff_26_q), .clk(clk), .Q(d_ff_31_q));  // open: Qn, preset, reset
  fiveClockDelay fiveclockdelay_1 (
    .DataIn({{16{1'b0}}, multiplexer_25_out, Address[5:4], register_53_q, 2'b00}), .clk(clk),
    .DataOut(fiveclockdelay_1_dataout));
  or or_6 (ReadFromMem, d_ff_11_q, d_ff_13_q, d_ff_16_q, d_ff_22_q);
  D_Flip_Flop d_ff_32 (.D(d_ff_22_q), .clk(clk), .Q(d_ff_32_q));  // open: Qn, preset, reset
  D_Flip_Flop d_ff_33 (.D(d_ff_28_q), .clk(clk), .Q(d_ff_33_q));  // open: Qn, preset, reset
  D_Flip_Flop d_ff_34 (.D(d_ff_31_q), .clk(clk), .Q(d_ff_34_q));  // open: Qn, preset, reset
  assign and_75_out = Address & 32'hfffffff3;  // AND_Gate and_75, 32 bits wide
  or or_7 (or_7_out, and_74_out, d_ff_18_q, d_ff_24_q, d_ff_29_q);
  or or_8 (WriteInMemory, Tmp_En, d_ff_19_q, d_ff_25_q, d_ff_30_q);
  D_Flip_Flop d_ff_35 (.D(d_ff_34_q), .clk(clk), .Q(d_ff_35_q));  // open: Qn, preset, reset
  or or_9 (or_9_out, and_73_out, d_ff_15_q, d_ff_21_q, d_ff_27_q);
  Register #(.width(2)) register_54 (.D(adder_5_out), .en(or_9_out), .clk(clk), .Q(register_54_q));  // open: clr
  Adder #(.width(32)) adder_2 (.a(and_75_out), .b(32'h4), .out(adder_2_out));  // open: cin, cout
  Adder #(.width(32)) adder_3 (.a(and_75_out), .b(32'h8), .out(adder_3_out));  // open: cin, cout
  Adder #(.width(32)) adder_4 (.a(and_75_out), .b(32'hc), .out(adder_4_out));  // open: cin, cout
  or or_10 (WE_select, d_ff_6_q, d_ff_8_q, d_ff_10_q, d_ff_12_q, d_ff_14_q, d_ff_17_q, d_ff_23_q, d_ff_28_q, d_ff_33_q);
  and and_76 (Last_WE, Tmp_writeEnable, d_ff_32_q);
  Register #(.width(2)) register_55 (.D(adder_6_out), .en(or_7_out), .clk(clk), .Q(register_55_q));  // open: clr
  D_Flip_Flop d_ff_36 (.D(d_ff_35_q), .clk(clk), .Q(d_ff_36_q));  // open: Qn, preset, reset
  Multiplexer #(.select(2), .width(32)) multiplexer_26 (
    .in0(and_75_out), .in1(adder_2_out), .in2(adder_3_out), .in3(adder_4_out), .out(multiplexer_26_out),
    .sel(register_54_q));
  Multiplexer #(.select(2), .width(32)) multiplexer_27 (
    .in0(multiplexer_21_out), .in1(multiplexer_22_out), .in2(multiplexer_23_out), .in3(multiplexer_24_out),
    .out(WriteDataOut), .sel(register_55_q));
  D_Flip_Flop d_ff_37 (.D(d_ff_36_q), .clk(clk), .Q(d_ff_37_q));  // open: Qn, preset, reset
  Adder #(.width(2)) adder_5 (.a(register_54_q), .b(2'b01), .out(adder_5_out));  // open: cin, cout
  Register #(.width(32)) register_56 (.D(multiplexer_26_out), .clk(clk), .Q(register_56_q));  // open: en, clr
  Adder #(.width(2)) adder_6 (.a(register_55_q), .b(2'b01), .out(adder_6_out));  // open: cin, cout
  D_Flip_Flop d_ff_38 (.D(d_ff_37_q), .clk(clk), .Q(d_ff_38_q));  // open: Qn, preset, reset
  Register #(.width(32)) register_57 (.D(register_56_q), .clk(clk), .Q(register_57_q));  // open: en, clr
  Register #(.width(32)) register_58 (.D(register_57_q), .clk(clk), .Q(register_58_q));  // open: en, clr
  Multiplexer #(.width(32)) multiplexer_28 (
    .in0(multiplexer_26_out), .in1(fiveclockdelay_1_dataout), .out(AddressOut), .sel(SetAddressOut));
  or or_11 (SetAddressOut, d_ff_35_q, d_ff_36_q, d_ff_37_q, d_ff_38_q);
  Register #(.width(32)) register_59 (.D(register_58_q), .clk(clk), .Q(register_59_q));  // open: en, clr
  Register #(.width(32)) register_60 (.D(register_59_q), .clk(clk), .Q(RFMAddress));  // open: en, clr

  // Other names for the same wires on the sheet: Set[1:0] = Address[5:4]; word[1:0] = Address[3:2];
  //   Tag[9:0] = Address[15:6]; Clock = clk; Tmp_writeData[31:0] = Last_W_Data

  // Notes on the sheet:
  //   Tag Enables
  //   Inputs
  //   Word Enables
  //   Outputs
  //   Validity Enables
  //   Tag
endmodule
