// Logisim project memDelayed.circ as structural Verilog: 1 circuit, main circuit memDelayed
module memDelayed (
  input  [31:0] MemAddress,
  input  [3:0] MemWriteMask,
  input  [31:0] MemWriteData,
  input  clk,
  output [31:0] MemReadData
);

  wire [3:0] delaymodule_1_p3, delaymodule_2_p3, delaymodule_3_p3, delaymodule_4_p3, delaymodule_5_p3,
       delaymodule_6_p3, delaymodule_7_p3, delaymodule_8_p3, delaymodule_9_p2;
  wire [7:0] DMEM_0_dout, DMEM_1_dout, DMEM_2_dout, DMEM_3_dout;

  // delayModule delaymodule_1: pin names not known; wires that end beside it: MemWriteData[3:0], clk, delaymodule_1_p3, clk
  // delayModule delaymodule_2: pin names not known; wires that end beside it: MemWriteData[7:4], clk, delaymodule_2_p3
  // delayModule delaymodule_3: pin names not known; wires that end beside it: MemWriteData[11:8], clk, delaymodule_3_p3
  // delayModule delaymodule_4: pin names not known; wires that end beside it: MemWriteData[15:12], clk, delaymodule_4_p3
  // delayModule delaymodule_5: pin names not known; wires that end beside it: MemWriteData[19:16], clk, delaymodule_5_p3
  // delayModule delaymodule_6: pin names not known; wires that end beside it: MemWriteData[23:20], clk, delaymodule_6_p3
  // delayModule delaymodule_7: pin names not known; wires that end beside it: MemWriteData[27:24], clk, delaymodule_7_p3
  // delayModule delaymodule_8: pin names not known; wires that end beside it: MemWriteData[31:28], clk, delaymodule_8_p3
  // delayModule delaymodule_9: pin names not known; wires that end beside it: MemWriteMask, delaymodule_9_p2
  RAM #(.addrWidth(14)) DMEM_0 (
    .addr(MemAddress[15:2]), .we(delaymodule_9_p2[0]), .oe(1'b1), .clk(clk),
    .din({delaymodule_2_p3, delaymodule_1_p3}), .dout(DMEM_0_dout));
  RAM #(.addrWidth(14)) DMEM_1 (
    .addr(MemAddress[15:2]), .we(delaymodule_9_p2[1]), .oe(1'b1), .clk(clk),
    .din({delaymodule_4_p3, delaymodule_3_p3}), .dout(DMEM_1_dout));
  RAM #(.addrWidth(14)) DMEM_2 (
    .addr(MemAddress[15:2]), .we(delaymodule_9_p2[2]), .oe(1'b1), .clk(clk),
    .din({delaymodule_6_p3, delaymodule_5_p3}), .dout(DMEM_2_dout));
  RAM #(.addrWidth(14)) DMEM_3 (
    .addr(MemAddress[15:2]), .we(delaymodule_9_p2[3]), .oe(1'b1), .clk(clk),
    .din({delaymodule_8_p3, delaymodule_7_p3}), .dout(DMEM_3_dout));
  // delayModuleOut delaymoduleout_1: pin names not known; wires that end beside it: DMEM_0_dout[3:0], clk, MemReadData[3:0]
  // delayModuleOut delaymoduleout_2: pin names not known; wires that end beside it: DMEM_0_dout[7:4], clk, MemReadData[7:4]
  // delayModuleOut delaymoduleout_3: pin names not known; wires that end beside it: DMEM_1_dout[3:0], clk, MemReadData[11:8]
  // delayModuleOut delaymoduleout_4: pin names not known; wires that end beside it: DMEM_1_dout[7:4], clk, MemReadData[15:12]
  // delayModuleOut delaymoduleout_5: pin names not known; wires that end beside it: DMEM_2_dout[3:0], clk, MemReadData[19:16]
  // delayModuleOut delaymoduleout_6: pin names not known; wires that end beside it: DMEM_2_dout[7:4], clk, MemReadData[23:20]
  // delayModuleOut delaymoduleout_7: pin names not known; wires that end beside it: DMEM_3_dout[3:0], clk, MemReadData[27:24]
  // delayModuleOut delaymoduleout_8: pin names not known; wires that end beside it: DMEM_3_dout[7:4], clk, MemReadData[31:28]
endmodule
