// Logisim project one_clock_delay.circ as structural Verilog: 1 circuit, main circuit oneClockDelay
module oneClockDelay (
  input  [31:0] DataIn,
  input  clk,
  output [31:0] DataOut
);

  D_Flip_Flop d_ff_1 (.D(DataIn[0]), .clk(clk), .Q(DataOut[0]));  // open: Qn, preset, reset
  D_Flip_Flop d_ff_2 (.D(DataIn[1]), .clk(clk), .Q(DataOut[1]));  // open: Qn, preset, reset
  D_Flip_Flop d_ff_3 (.D(DataIn[2]), .clk(clk), .Q(DataOut[2]));  // open: Qn, preset, reset
  D_Flip_Flop d_ff_4 (.D(DataIn[3]), .clk(clk), .Q(DataOut[3]));  // open: Qn, preset, reset
  D_Flip_Flop d_ff_5 (.D(DataIn[4]), .clk(clk), .Q(DataOut[4]));  // open: Qn, preset, reset
  D_Flip_Flop d_ff_6 (.D(DataIn[5]), .clk(clk), .Q(DataOut[5]));  // open: Qn, preset, reset
  D_Flip_Flop d_ff_7 (.D(DataIn[6]), .clk(clk), .Q(DataOut[6]));  // open: Qn, preset, reset
  D_Flip_Flop d_ff_8 (.D(DataIn[7]), .clk(clk), .Q(DataOut[7]));  // open: Qn, preset, reset
  D_Flip_Flop d_ff_9 (.D(DataIn[8]), .clk(clk), .Q(DataOut[8]));  // open: Qn, preset, reset
  D_Flip_Flop d_ff_10 (.D(DataIn[9]), .clk(clk), .Q(DataOut[9]));  // open: Qn, preset, reset
  D_Flip_Flop d_ff_11 (.D(DataIn[10]), .clk(clk), .Q(DataOut[10]));  // open: Qn, preset, reset
  D_Flip_Flop d_ff_12 (.D(DataIn[11]), .clk(clk), .Q(DataOut[11]));  // open: Qn, preset, reset
  D_Flip_Flop d_ff_13 (.D(DataIn[12]), .clk(clk), .Q(DataOut[12]));  // open: Qn, preset, reset
  D_Flip_Flop d_ff_14 (.D(DataIn[13]), .clk(clk), .Q(DataOut[13]));  // open: Qn, preset, reset
  D_Flip_Flop d_ff_15 (.D(DataIn[14]), .clk(clk), .Q(DataOut[14]));  // open: Qn, preset, reset
  D_Flip_Flop d_ff_16 (.D(DataIn[15]), .clk(clk), .Q(DataOut[15]));  // open: Qn, preset, reset
  D_Flip_Flop d_ff_17 (.D(DataIn[16]), .clk(clk), .Q(DataOut[16]));  // open: Qn, preset, reset
  D_Flip_Flop d_ff_18 (.D(DataIn[17]), .clk(clk), .Q(DataOut[17]));  // open: Qn, preset, reset
  D_Flip_Flop d_ff_19 (.D(DataIn[18]), .clk(clk), .Q(DataOut[18]));  // open: Qn, preset, reset
  D_Flip_Flop d_ff_20 (.D(DataIn[19]), .clk(clk), .Q(DataOut[19]));  // open: Qn, preset, reset
  D_Flip_Flop d_ff_21 (.D(DataIn[20]), .clk(clk), .Q(DataOut[20]));  // open: Qn, preset, reset
  D_Flip_Flop d_ff_22 (.D(DataIn[21]), .clk(clk), .Q(DataOut[21]));  // open: Qn, preset, reset
  D_Flip_Flop d_ff_23 (.D(DataIn[22]), .clk(clk), .Q(DataOut[22]));  // open: Qn, preset, reset
  D_Flip_Flop d_ff_24 (.D(DataIn[23]), .clk(clk), .Q(DataOut[23]));  // open: Qn, preset, reset
  D_Flip_Flop d_ff_25 (.D(DataIn[24]), .clk(clk), .Q(DataOut[24]));  // open: Qn, preset, reset
  D_Flip_Flop d_ff_26 (.D(DataIn[25]), .clk(clk), .Q(DataOut[25]));  // open: Qn, preset, reset
  D_Flip_Flop d_ff_27 (.D(DataIn[26]), .clk(clk), .Q(DataOut[26]));  // open: Qn, preset, reset
  D_Flip_Flop d_ff_28 (.D(DataIn[27]), .clk(clk), .Q(DataOut[27]));  // open: Qn, preset, reset
  D_Flip_Flop d_ff_29 (.D(DataIn[28]), .clk(clk), .Q(DataOut[28]));  // open: Qn, preset, reset
  D_Flip_Flop d_ff_30 (.D(DataIn[29]), .clk(clk), .Q(DataOut[29]));  // open: Qn, preset, reset
  D_Flip_Flop d_ff_31 (.D(DataIn[30]), .clk(clk), .Q(DataOut[30]));  // open: Qn, preset, reset
  D_Flip_Flop d_ff_32 (.D(DataIn[31]), .clk(clk), .Q(DataOut[31]));  // open: Qn, preset, reset
endmodule
