// Logisim project singExtender.circ as structural Verilog: 1 circuit, main circuit signExtend
module signExtend (
  input  [15:0] Immd,
  output [31:0] Extended
);

  assign Extended = {{16{Immd[15]}}, Immd};  // Bit_Extender bit_extender_1
endmodule
